// Logisim project Tomlin_Nathan_Maloul_Layth_P1.circ as structural Verilog: 1 circuit, main circuit main
module main (
  input  X3,
  input  X2,
  input  X1,
  input  X0
);

  wire and_1_out, and_2_out, and_3_out, and_4_out, and_5_out, and_6_out, and_7_out, and_8_out, and_9_out,
       not_1_out, not_2_out, not_3_out, not_4_out;
  wire [3:0] xor_1_out;

  not not_1 (not_1_out, X3);
  not not_2 (not_2_out, X2);
  not not_3 (not_3_out, X1);
  not not_4 (not_4_out, X0);
  and and_1 (and_1_out, X0, not_3_out, not_2_out);
  and and_2 (and_2_out, not_4_out, X1, not_2_out);
  and and_3 (and_3_out, X0, X2, not_1_out);
  and and_4 (and_4_out, not_3_out, X2, X3);
  and and_5 (and_5_out, X1, X3);
  and and_6 (and_6_out, not_1_out, not_2_out, X1);
  and and_7 (and_7_out, not_2_out, not_3_out, X0);
  and and_8 (and_8_out, not_1_out, X2);
  and and_9 (and_9_out, not_2_out, X0);
  xor xor_1 (xor_1_out[0], X3, X2, X1, X0);
  or or_1 (xor_1_out[1], and_1_out, and_2_out, and_3_out, and_4_out);
  or or_2 (xor_1_out[2], and_5_out, and_6_out, and_7_out);
  or or_3 (xor_1_out[3], and_8_out, and_9_out);
  Hex_Digit_Display hex_digit_display_1 (.value(xor_1_out));  // open: dp

  // Notes on the sheet:
  //   X3X1
  //   PROJECT 1
  //   NATHAN TOMLIN & LAYTH MALOUL 
  //   MARCH 6th 2022
  //   X2'X1'X0
  //   X2'X1X0'
  //   X3'X2X0
  //   X3X2X1'
  //   X3'X2'X1
  //   X2'X1'X0
  //   X3'X2
  //   X2'X0
  //   Y0
  //   Y1
  //   Y2
  //   Y3
  //   X3'X2 + X2'X0
  //   Hex Display
  //   X2'X1'X0 + X2'X1X0' + X3'X2X0 + X3X2X1'
  //   X3X1 + X3'X2'X1 + X2'X1'X0
  //   Splitter
endmodule
